# Fritzing sketch 9v button (saved by Fritzing 1.0.6)
breadboards: 1

parts:
  S2 = Pushbutton [package="[SMD]"]
  VCC2 = Battery block 9V [internal_resistance=0.1Ω]
  LED2 = LED - 5mm [color="Red (633nm)" current=0.030A package="5 mm [THT]"]
  R2 = Resistor [tolerance=±5% resistance=330 power=0.25W package=THT]

nets:
  N1: S2.Pin_1, S2.Pin_2, R2.Pin_0
  N2: S2.Pin_3, S2.Pin_4, LED2.anode
  N3: VCC2.-, LED2.cathode
  N4: VCC2.+, R2.Pin_1
